# Fritzing sketch diatonic_Theremin (saved by Fritzing 0.9.3b)
breadboards: 1

parts:
  Componente1 = Arduino Mega 2560 (Rev3)
  botón_de_calibración = Pushbutton [package="[THT]"]
  R1 = Resistor [tolerance=±5% resistance=10k package=THT]
  R2 = Photocell (LDR) [package=THT]
  R3 = Resistor [tolerance=±5% resistance=1k package=THT]
  R5 = Resistor [tolerance=±5% resistance=330 package=THT]
  Botón_de_cambio_de_escala = Pushbutton [package="[THT]"]
  R6 = Resistor [tolerance=±5% resistance=10k package=THT]
  J1 = Piezo Speaker
  control_de_volumen = Trimmer Potentiometer [package=THT]

nets:
  N1: Componente1.D9_PWM, botón_de_calibración.Pin_1, botón_de_calibración.Pin_2, R1.Pin_0
  N2: Componente1.D8_PWM, control_de_volumen.leg2
  N3: Componente1.5V, botón_de_calibración.Pin_3, botón_de_calibración.Pin_4, R2.pin_0, Botón_de_cambio_de_escala.Pin_1, Botón_de_cambio_de_escala.Pin_2
  N4: Componente1.GND, R1.Pin_1, R3.Pin_1, R6.Pin_0, J1.pin2, control_de_volumen.leg1
  N5: Componente1.D7_PWM, Botón_de_cambio_de_escala.Pin_3, Botón_de_cambio_de_escala.Pin_4, R6.Pin_1
  N6: R2.pin_1, R3.Pin_0
  N7: R5.Pin_0, control_de_volumen.wiper
  N8: R5.Pin_1, J1.pin1
